# Fritzing sketch Particle-Photon-DHT22 (saved by Fritzing 0.9.2b)
breadboards: 1

parts:
  U1 = Spark Core (v1.0)
  RHT1 = Humidity and Temperature Sensor RHT03
  R1 = Resistor [tolerance=±5% resistance=3.5k package="2010 [SMD]"]

nets:
  N1: U1.A2, U1.3V3
  N2: U1.A3, U1.A6
  N3: U1.A5, U1.VIN
  N4: U1.D3, RHT1.Data-signal
  N5: U1.3V3*, RHT1.Vcc, R1.Pin_1
  N6: RHT1.GND_1, R1.Pin_0

notes:
  3.5kOhm pull-up resistance

custom parts:
  Spark Core (v1.0): The Spark Core is a tiny Wi-Fi development board that makes it easy to create internet-connected hardware. The Core is all you need to get started; power it over USB and in minutes you'll be controlling LEDs, switches and motors and collecting data from sensors over the internet! It has 8 digital I/O pins, 8 analog I/O pins, 8 PWM pins; UART (Serial), SPI, I2C, and JTAG peripherals available.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
